// Logisim project Lab_1.circ as structural Verilog: 1 circuit, main circuit main
module main (
  input  [2:0] decoder_select,
  input  [3:0] multiplexer_input,
  input  [1:0] multiplexer_select,
  output [7:0] decoder_output,
  output multiplexer_output
);

  wire and_9_out, and_10_out, and_11_out, and_12_out, not_1_out, not_2_out, not_3_out, not_4_out, not_5_out,
       not_6_out, not_7_out, not_8_out, not_9_out, not_10_out, not_11_out, not_12_out, not_13_out, not_14_out;

  not not_1 (not_1_out, multiplexer_select[0]);
  not not_2 (not_2_out, multiplexer_select[1]);
  not not_3 (not_3_out, decoder_select[0]);
  not not_4 (not_4_out, decoder_select[1]);
  and and_1 (decoder_output[0], not_3_out, not_4_out, not_5_out);
  not not_5 (not_5_out, decoder_select[2]);
  not not_6 (not_6_out, decoder_select[0]);
  and and_2 (decoder_output[2], not_6_out, decoder_select[1], not_7_out);
  not not_7 (not_7_out, decoder_select[2]);
  and and_3 (decoder_output[7], decoder_select[0], decoder_select[1], decoder_select[2]);
  not not_8 (not_8_out, decoder_select[1]);
  and and_4 (decoder_output[1], decoder_select[0], not_8_out, not_9_out);
  not not_9 (not_9_out, decoder_select[2]);
  and and_5 (decoder_output[3], decoder_select[0], decoder_select[1], not_10_out);
  not not_10 (not_10_out, decoder_select[2]);
  and and_6 (decoder_output[5], decoder_select[0], decoder_select[2], not_11_out);
  not not_11 (not_11_out, decoder_select[1]);
  not not_12 (not_12_out, decoder_select[0]);
  not not_13 (not_13_out, decoder_select[1]);
  and and_7 (decoder_output[4], not_12_out, not_13_out, decoder_select[2]);
  and and_8 (decoder_output[6], decoder_select[2], decoder_select[1], not_14_out);
  not not_14 (not_14_out, decoder_select[0]);
  and and_9 (and_9_out, multiplexer_input[0], not_1_out, not_2_out);
  and and_10 (and_10_out, multiplexer_input[1], multiplexer_select[0], not_2_out);
  and and_11 (and_11_out, multiplexer_input[2], not_1_out, multiplexer_select[1]);
  and and_12 (and_12_out, multiplexer_input[3], multiplexer_select[0], multiplexer_select[1]);
  or or_1 (multiplexer_output, and_9_out, and_10_out, and_11_out, and_12_out);

  // Notes on the sheet:
  //   Decoder Circuit
  //   Multiplexer Circuit
endmodule
