// Logisim project Lab_2.circ as structural Verilog: 1 circuit, main circuit main
module main (
  input  [3:0] ALU_input_a,
  input  [3:0] ALU_input_b,
  input  [1:0] ALU_select,
  output [3:0] ALU_output,
  output ADD_carry
);

  wire and_5_out, and_6_out, and_7_out, and_8_out, or_1_out, or_2_out, xnor_1_out, xnor_2_out, xnor_3_out,
       xnor_4_out, xor_1_out, xor_2_out, xor_3_out;
  wire [3:0] and_4_out, and_9_out, and_10_out, and_11_out, nnot_p4, not_5_out, xor_4_out;
  wire [3:3] not_3_out, not_6_out, not_7_out;

  and and_1 (and_4_out[1], ALU_input_a[1], ALU_input_b[1]);
  and and_2 (and_4_out[2], ALU_input_a[2], ALU_input_b[2]);
  xor xor_1 (xor_1_out, ALU_input_a[1], ALU_input_b[1]);
  xor xor_2 (xor_2_out, ALU_input_b[2], ALU_input_a[2]);
  xor xor_3 (xor_3_out, ALU_input_a[3], ALU_input_b[3]);
  and and_3 (and_4_out[3], ALU_input_a[3], ALU_input_b[3]);
  xnor xnor_1 (xnor_1_out, ALU_input_b[0], ALU_input_a[0]);
  xnor xnor_2 (xnor_2_out, ALU_input_b[1], ALU_input_a[1]);
  xnor xnor_3 (xnor_3_out, ALU_input_b[2], ALU_input_a[2]);
  xnor xnor_4 (xnor_4_out, ALU_input_b[3], ALU_input_a[3]);
  xor xor_4 (xor_4_out[0], ALU_input_a[0], ALU_input_b[0]);
  and and_4 (and_4_out[0], ALU_input_a[0], ALU_input_b[0]);
  xor xor_5 (xor_4_out[1], xor_1_out, and_4_out[0]);
  and and_5 (and_5_out, xor_1_out, and_4_out[0]);
  xor xor_6 (xor_4_out[2], or_1_out, xor_2_out);
  and and_6 (and_6_out, xor_2_out, or_1_out);
  xor xor_7 (xor_4_out[3], or_2_out, xor_3_out);
  or or_1 (or_1_out, and_5_out, and_4_out[1]);
  or or_2 (or_2_out, and_6_out, and_4_out[2]);
  and and_7 (and_7_out, or_2_out, xor_3_out);
  or or_3 (ADD_carry, and_7_out, and_4_out[3]);
  and and_8 (and_8_out, xnor_1_out, xnor_2_out, xnor_3_out, xnor_4_out);
  not not_1 (not_5_out[2], ALU_input_a[2]);
  not not_2 (not_5_out[3], ALU_input_a[3]);
  not not_3 (not_3_out[3], and_8_out);
  not not_4 (not_5_out[1], ALU_input_a[1]);
  not not_5 (not_5_out[0], ALU_input_a[0]);
  not not_6 (not_6_out[3], ALU_select[0]);
  not not_7 (not_7_out[3], ALU_select[1]);
  // AND_Gate #(.width(4)) nnot: pin names not known; wires that end beside it: not_5_out, {4{not_6_out[3]}}, {4{ALU_select[1]}}, nnot_p4
  assign and_9_out = xor_4_out & {4{not_6_out[3]}} & {4{not_7_out[3]}};  // AND_Gate and_9, 4 bits wide
  assign and_10_out = and_4_out & {4{not_7_out[3]}};  // AND_Gate and_10, 4 bits wide
  assign and_11_out = {4{not_3_out[3]}} & {4{ALU_select[0]}} & {4{ALU_select[1]}};  // AND_Gate and_11, 4 bits wide
  assign ALU_output = nnot_p4 | and_9_out | and_10_out | and_11_out;  // OR_Gate or_4, 4 bits wide
endmodule
