// Logisim project lab_2_template.circ as structural Verilog: 1 circuit, main circuit main
module main (
  input  [3:0] ALU_input_a,
  input  [3:0] ALU_input_b,
  input  [1:0] ALU_select,
  output [3:0] ALU_output,
  output ADD_carry
);

  wire and_5_out, and_6_out, and_7_out, or_1_out, or_2_out, xor_1_out, xor_2_out, xor_3_out;
  wire [3:0] and_4_out, not_4_out, xor_6_out;

  and and_1 (and_4_out[1], ALU_input_a[1], ALU_input_b[1]);
  xor xor_1 (xor_1_out, ALU_input_a[1], ALU_input_b[1]);
  xor xor_2 (xor_2_out, ALU_input_b[2], ALU_input_a[2]);
  and and_2 (and_4_out[2], ALU_input_a[2], ALU_input_b[2]);
  xor xor_3 (xor_3_out, ALU_input_a[3], ALU_input_b[3]);
  and and_3 (and_4_out[3], ALU_input_a[3], ALU_input_b[3]);
  and and_4 (and_4_out[0], ALU_input_a[0], ALU_input_b[0]);
  xor xor_4 (xor_6_out[1], xor_1_out, and_4_out[0]);
  xor xor_5 (xor_6_out[2], or_1_out, xor_2_out);
  xor xor_6 (xor_6_out[0], ALU_input_a[0], ALU_input_b[0]);
  and and_5 (and_5_out, xor_1_out, and_4_out[0]);
  and and_6 (and_6_out, xor_2_out, or_1_out);
  xor xor_7 (xor_6_out[3], or_2_out, xor_3_out);
  or or_1 (or_1_out, and_5_out, and_4_out[1]);
  or or_2 (or_2_out, and_6_out, and_4_out[2]);
  and and_7 (and_7_out, or_2_out, xor_3_out);
  not not_1 (not_4_out[3], ALU_input_a[3]);
  or or_3 (ADD_carry, and_7_out, and_4_out[3]);
  not not_2 (not_4_out[2], ALU_input_a[2]);
  not not_3 (not_4_out[1], ALU_input_a[1]);
  not not_4 (not_4_out[0], ALU_input_a[0]);
endmodule
